// Logisim project 3-8.circ as structural Verilog: 1 circuit, main circuit main
module main (
  input  Z,
  input  Y,
  input  X,
  output D0,
  output D1,
  output D2,
  output D3,
  output D4,
  output D5,
  output D6,
  output D7
);

  wire not_1_out, not_2_out, not_3_out;

  not not_1 (not_1_out, Z);
  not not_2 (not_2_out, Y);
  not not_3 (not_3_out, X);
  and and_1 (D0, not_1_out, not_2_out, not_3_out);
  and and_2 (D1, Z, not_2_out, not_3_out);
  and and_3 (D2, not_1_out, Y, not_3_out);
  and and_4 (D3, Z, Y, not_3_out);
  and and_5 (D4, not_1_out, not_2_out, X);
  and and_6 (D5, Z, not_2_out, X);
  and and_7 (D6, not_1_out, Y, X);
  and and_8 (D7, Z, Y, X);

  // Notes on the sheet:
  //   3-8 DECODER
endmodule
