// Logisim project 8-3.circ as structural Verilog: 1 circuit, main circuit main
module main (
  input  D7,
  input  D6,
  input  D5,
  input  D4,
  input  D3,
  input  D2,
  input  D1,
  input  D0,
  output X,
  output Y,
  output Z
);

  or or_1 (X, D7, D6, D5, D4);
  or or_2 (Y, D7, D6, D3, D2);
  or or_3 (Z, D7, D5, D3, D1);

  // Notes on the sheet:
  //   8-3 ENCODER CIRCUIT
endmodule
