// Logisim project ALU.circ as structural Verilog: 2 circuits, main circuit 1b ALU
module _1b_ALU (
  input  [2:0] in_1,
  input  Sub,
  input  Cin,
  input  A,
  input  B,
  input  Less,
  output out_7,
  output Cout,
  output Set
);

  wire and_1_out, nor_1_out, or_1_out, xor_1_out, xor_2_out;

  xor xor_1 (xor_1_out, B, Sub);
  and and_1 (and_1_out, A, B);
  or or_1 (or_1_out, A, B);
  xor xor_2 (xor_2_out, A, B);
  nor nor_1 (nor_1_out, A, B);
  Adder #(.width(1)) adder_1 (.a(A), .b(xor_1_out), .out(Set), .cin(Cin), .cout(Cout));
  Multiplexer #(.select(3), .enable("false")) multiplexer_1 (
    .in0(and_1_out), .in1(or_1_out), .in2(xor_2_out), .in3(nor_1_out), .in4(Set), .in5(Less), .out(out_7),
    .sel(in_1));  // open: in6, in7
endmodule

module ALU (
  input  Sub,
  input  [2:0] OP,
  input  [7:0] A,
  input  [7:0] B,
  output [7:0] R,
  output zero
);

  wire n1b_alu_1_cout, n1b_alu_2_cout, n1b_alu_3_cout, n1b_alu_4_cout, n1b_alu_5_cout, n1b_alu_6_cout,
       n1b_alu_7_cout, n1b_alu_8_set;

  _1b_ALU u_1b_alu_1 (
    .A(A[0]), .B(B[0]), .Less(n1b_alu_8_set), .out_7(R[0]), .Sub(Sub), .Cin(Sub), .in_1(OP),
    .Cout(n1b_alu_1_cout));  // open: Set
  _1b_ALU u_1b_alu_2 (
    .A(A[1]), .B(B[1]), .Less(1'b0), .out_7(R[1]), .Sub(Sub), .Cin(n1b_alu_1_cout), .in_1(OP),
    .Cout(n1b_alu_2_cout));  // open: Set
  _1b_ALU u_1b_alu_3 (
    .A(A[2]), .B(B[2]), .Less(1'b0), .out_7(R[2]), .Sub(Sub), .Cin(n1b_alu_2_cout), .in_1(OP),
    .Cout(n1b_alu_3_cout));  // open: Set
  _1b_ALU u_1b_alu_4 (
    .A(A[3]), .B(B[3]), .Less(1'b0), .out_7(R[3]), .Sub(Sub), .Cin(n1b_alu_3_cout), .in_1(OP),
    .Cout(n1b_alu_4_cout));  // open: Set
  _1b_ALU u_1b_alu_5 (
    .A(A[4]), .B(B[4]), .Less(1'b0), .out_7(R[4]), .Sub(Sub), .Cin(n1b_alu_4_cout), .in_1(OP),
    .Cout(n1b_alu_5_cout));  // open: Set
  _1b_ALU u_1b_alu_6 (
    .A(A[5]), .B(B[5]), .Less(1'b0), .out_7(R[5]), .Sub(Sub), .Cin(n1b_alu_5_cout), .in_1(OP),
    .Cout(n1b_alu_6_cout));  // open: Set
  _1b_ALU u_1b_alu_7 (
    .A(A[6]), .B(B[6]), .Less(1'b0), .out_7(R[6]), .Sub(Sub), .Cin(n1b_alu_6_cout), .in_1(OP),
    .Cout(n1b_alu_7_cout));  // open: Set
  _1b_ALU u_1b_alu_8 (
    .A(A[7]), .B(B[7]), .Less(1'b0), .out_7(R[7]), .Sub(Sub), .Cin(n1b_alu_7_cout), .in_1(OP),
    .Set(n1b_alu_8_set));  // open: Cout
  nor nor_1 (zero, R[0], R[1], R[2], R[3], R[4], R[5], R[6], R[7]);
endmodule
