// Logisim project Carry Look-Ahead Adder.circ as structural Verilog: 1 circuit, main circuit main
module main (
  input  P3,
  input  G3,
  input  P2,
  input  G2,
  input  P1,
  input  G1,
  input  C1,
  output C4,
  output C3,
  output C2
);

  wire and_1_out, and_2_out, and_3_out, and_4_out, and_5_out, and_6_out;

  and and_1 (and_1_out, C1, P1, P2, P3);
  and and_2 (and_2_out, G1, P2, P3);
  and and_3 (and_3_out, G2, P3);
  and and_4 (and_4_out, C1, P1, P2);
  and and_5 (and_5_out, G1, P2);
  and and_6 (and_6_out, C1, P1);
  or or_1 (C4, and_1_out, and_2_out, and_3_out, G3);
  or or_2 (C3, and_4_out, and_5_out, G2);
  or or_3 (C2, and_6_out, G1);

  // Notes on the sheet:
  //   Carry Look-Ahead Adder
endmodule
