// Logisim project D Flip-Flop.circ as structural Verilog: 1 circuit, main circuit main
module main (
  input  D,
  output Qn,
  output Qn_prime
);

  wire and_1_out, and_2_out, clock_1_out, not_1_out;

  not not_1 (not_1_out, D);
  Clock clock_1 (.out(clock_1_out));
  and and_1 (and_1_out, not_1_out, clock_1_out);
  and and_2 (and_2_out, clock_1_out, not_1_out);
  nor nor_1 (Qn, and_1_out, Qn_prime);
  nor nor_2 (Qn_prime, Qn, and_2_out);

  // Notes on the sheet:
  //   Clock Pulse
  //   D Flip-Flop
endmodule
