// Logisim project FULL ADDER CIRCUIT PART-1.circ as structural Verilog: 1 circuit, main circuit main
module main (
  input  A,
  input  A_2,
  input  B,
  input  B_2,
  input  Cin,
  input  Cin_2,
  input  A_3,
  input  A_4,
  input  B_3,
  input  B_4,
  input  Cin_3,
  input  Cin_4,
  output SUM,
  output SUM_2,
  output CARRY,
  output CARRY_2,
  output SUM_3,
  output SUM_4,
  output CARRY_3,
  output CARRY_4
);

  wire and_1_out, and_2_out, and_3_out, and_4_out, and_5_out, and_6_out, and_7_out, and_8_out, xor_1_out,
       xor_2_out, xor_5_out, xor_6_out;

  xor xor_1 (xor_1_out, A, B);
  xor xor_2 (xor_2_out, A_3, B_3);
  and and_1 (and_1_out, Cin, xor_1_out);
  and and_2 (and_2_out, A, B);
  and and_3 (and_3_out, Cin_3, xor_2_out);
  and and_4 (and_4_out, A_3, B_3);
  xor xor_3 (SUM, xor_1_out, Cin);
  xor xor_4 (SUM_3, xor_2_out, Cin_3);
  or or_1 (CARRY, and_1_out, and_2_out);
  or or_2 (CARRY_3, and_3_out, and_4_out);
  xor xor_5 (xor_5_out, A_2, B_2);
  xor xor_6 (xor_6_out, A_4, B_4);
  and and_5 (and_5_out, Cin_2, xor_5_out);
  and and_6 (and_6_out, A_2, B_2);
  and and_7 (and_7_out, Cin_4, xor_6_out);
  and and_8 (and_8_out, A_4, B_4);
  xor xor_7 (SUM_2, xor_5_out, Cin_2);
  xor xor_8 (SUM_4, xor_6_out, Cin_4);
  or or_3 (CARRY_2, and_5_out, and_6_out);
  or or_4 (CARRY_4, and_7_out, and_8_out);
  // NOT_Gate not_1 is placed but not wired

  // Notes on the sheet:
  //   Full Adder Circuit
endmodule
