// Logisim project HALF ADDER CIRCUIT.circ as structural Verilog: 1 circuit, main circuit main
module main (
  input  in_1,
  input  in_2,
  input  in_3,
  input  in_4,
  input  in_5,
  input  in_6,
  input  in_7,
  input  in_8,
  output Carry,
  output Carry_2,
  output Sum,
  output Sum_2,
  output Carry_3,
  output Carry_4,
  output Sum_3,
  output Sum_4
);

  and and_1 (Carry, in_1, in_3);
  xor xor_1 (Sum, in_1, in_3);
  and and_2 (Carry_3, in_5, in_7);
  xor xor_2 (Sum_3, in_5, in_7);
  and and_3 (Carry_2, in_2, in_4);
  xor xor_3 (Sum_2, in_2, in_4);
  and and_4 (Carry_4, in_6, in_8);
  xor xor_4 (Sum_4, in_6, in_8);

  // Notes on the sheet:
  //   Half Adder Circuit
endmodule
