// Logisim project NAND AS NOT GATE.circ as structural Verilog: 1 circuit, main circuit main
module main (
  input  in_1,
  input  in_2,
  output out_3,
  output out_4
);

  nand nand_1 (out_3, in_1, in_1);
  nand nand_2 (out_4, in_2, in_2);

  // Notes on the sheet:
  //   NAND Gate as NOT Gate
endmodule
