// Logisim project NAND AS OR GATE.circ as structural Verilog: 1 circuit, main circuit main
module main (
  input  in_1,
  input  in_2,
  input  in_3,
  input  in_4,
  input  in_5,
  input  in_6,
  input  in_7,
  input  in_8,
  output out_9,
  output out_10,
  output out_11,
  output out_12
);

  wire nand_1_out, nand_2_out, nand_3_out, nand_4_out, nand_7_out, nand_8_out, nand_9_out, nand_10_out;

  nand nand_1 (nand_1_out, in_1, in_1);
  nand nand_2 (nand_2_out, in_3, in_3);
  nand nand_3 (nand_3_out, in_5, in_5);
  nand nand_4 (nand_4_out, in_7, in_7);
  nand nand_5 (out_9, nand_1_out, nand_2_out);
  nand nand_6 (out_11, nand_3_out, nand_4_out);
  nand nand_7 (nand_7_out, in_2, in_2);
  nand nand_8 (nand_8_out, in_4, in_4);
  nand nand_9 (nand_9_out, in_6, in_6);
  nand nand_10 (nand_10_out, in_8, in_8);
  nand nand_11 (out_10, nand_7_out, nand_8_out);
  nand nand_12 (out_12, nand_9_out, nand_10_out);

  // Notes on the sheet:
  //   NAND Gate as OR Gate
endmodule
