// Logisim project NAND GATE.circ as structural Verilog: 1 circuit, main circuit main
module main (
  input  in_1,
  input  NAND_Gate,
  input  in_3,
  input  in_4,
  input  in_5,
  input  in_6,
  input  in_7,
  input  in_8,
  output out_9,
  output out_10,
  output out_11,
  output out_12
);

  nand nand_1 (out_9, in_1, in_3);
  nand nand_2 (out_11, in_5, in_7);
  nand nand_3 (out_10, NAND_Gate, in_4);
  nand nand_4 (out_12, in_6, in_8);
endmodule
