// Logisim project NOR AS AND GATE.circ as structural Verilog: 1 circuit, main circuit main
module main (
  input  in_1,
  input  in_2,
  input  in_3,
  input  in_4,
  input  in_5,
  input  in_6,
  input  in_7,
  input  in_8,
  output out_9,
  output out_10,
  output out_11,
  output out_12
);

  wire nor_1_out, nor_2_out, nor_3_out, nor_4_out, nor_7_out, nor_8_out, nor_9_out, nor_10_out;

  nor nor_1 (nor_1_out, in_1, in_1);
  nor nor_2 (nor_2_out, in_3, in_3);
  nor nor_3 (nor_3_out, in_5, in_5);
  nor nor_4 (nor_4_out, in_7, in_7);
  nor nor_5 (out_9, nor_1_out, nor_2_out);
  nor nor_6 (out_11, nor_3_out, nor_4_out);
  nor nor_7 (nor_7_out, in_2, in_2);
  nor nor_8 (nor_8_out, in_4, in_4);
  nor nor_9 (nor_9_out, in_6, in_6);
  nor nor_10 (nor_10_out, in_8, in_8);
  nor nor_11 (out_10, nor_7_out, nor_8_out);
  nor nor_12 (out_12, nor_9_out, nor_10_out);

  // Notes on the sheet:
  //   NOR Gate as AND Gate
endmodule
