// Logisim project NOR AS OR GATE.circ as structural Verilog: 1 circuit, main circuit main
module main (
  input  in_1,
  input  in_2,
  input  in_3,
  input  in_4,
  input  in_5,
  input  in_6,
  input  in_7,
  input  in_8,
  output out_9,
  output out_10,
  output out_11,
  output out_12
);

  wire nor_1_out, nor_2_out, nor_5_out, nor_6_out;

  nor nor_1 (nor_1_out, in_1, in_3);
  nor nor_2 (nor_2_out, in_5, in_7);
  nor nor_3 (out_9, nor_1_out, nor_1_out);
  nor nor_4 (out_11, nor_2_out, nor_2_out);
  nor nor_5 (nor_5_out, in_2, in_4);
  nor nor_6 (nor_6_out, in_6, in_8);
  nor nor_7 (out_10, nor_5_out, nor_5_out);
  nor nor_8 (out_12, nor_6_out, nor_6_out);

  // Notes on the sheet:
  //   NOR Gate as OR Gate
endmodule
