// Logisim project SR Flip-Flop.circ as structural Verilog: 1 circuit, main circuit main
module main (
  input  R,
  input  S,
  input  R_2,
  input  S_2,
  output Qn,
  output Qn_prime,
  output Qn_2,
  output Qn_prime_2
);

  wire and_1_out, and_2_out, clock_1_out, clock_2_out, nand_1_out, nand_2_out;

  Clock clock_1 (.out(clock_1_out));
  Clock clock_2 (.out(clock_2_out));
  and and_1 (and_1_out, R, clock_1_out);
  and and_2 (and_2_out, clock_1_out, S);
  nand nand_1 (nand_1_out, R_2, clock_2_out);
  nand nand_2 (nand_2_out, clock_2_out, S_2);
  nor nor_1 (Qn, and_1_out, Qn_prime);
  nor nor_2 (Qn_prime, Qn, and_2_out);
  nand nand_3 (Qn_2, nand_1_out, Qn_prime_2);
  nand nand_4 (Qn_prime_2, Qn_2, nand_2_out);

  // Notes on the sheet:
  //   Clock Pulse
  //   Clock Pulse
  //   SR Flip-Flop
  //   NOR Latch
  //   NAND Latch
endmodule
