// Logisim project pipo.circ as structural Verilog: 2 circuits, main circuit D-type-FF
module D_type_FF (
  input  CK,
  input  D0,
  input  D1,
  input  D2,
  input  D3,
  output Q0,
  output Q1,
  output Q2,
  output Q3
);

  main main_1 (.D(D1), .CK(CK), .Q(Q1));  // open: nQ
  main main_2 (.D(D0), .CK(CK), .Q(Q0));  // open: nQ
  main main_3 (.D(D2), .CK(CK), .Q(Q2));  // open: nQ
  main main_4 (.D(D3), .CK(CK), .Q(Q3));  // open: nQ

  // Notes on the sheet:
  //   PIPO
endmodule

module main (
  input  D,
  input  CK,
  output Q,
  output nQ
);

  wire and_1_out, buffer_1_out, nand_1_out, nand_2_out, not_1_out, not_2_out;

  not not_1 (not_1_out, buffer_1_out);
  buf buffer_1 (buffer_1_out, CK);
  and and_1 (and_1_out, CK, not_1_out);
  nand nand_1 (nand_1_out, D, and_1_out);
  nand nand_2 (nand_2_out, and_1_out, not_2_out);
  not not_2 (not_2_out, D);
  nand nand_3 (Q, nand_1_out, nQ);
  nand nand_4 (nQ, Q, nand_2_out);

  // Notes on the sheet:
  //   Positive Edge Triggered D Type Flip-flop
  //   www.learnabout-electronics.org
endmodule
