// Logisim project piso.circ as structural Verilog: 2 circuits, main circuit main
module main (
  input  INPUT,
  input  CK,
  input  nLOAD,
  input  D0,
  input  D1,
  input  D2,
  input  D3,
  output Q0,
  output Q1,
  output Q2,
  output Q3,
  output out_12
);

  wire jk_1_nq, jk_2_nq, jk_3_nq, nand_1_out, nand_2_out, nand_3_out, nand_4_out, nand_5_out, nand_6_out,
       nand_7_out, nand_8_out, not_1_out, not_2_out, not_3_out, not_4_out, not_5_out, not_6_out;

  not not_1 (not_1_out, INPUT);
  not not_2 (not_2_out, nLOAD);
  JK jk_1 (.J(INPUT), .CK(CK), .K(not_1_out), .nPR(nand_1_out), .nCLR(nand_2_out), .Q(Q0), .nQ(jk_1_nq));
  nand nand_1 (nand_1_out, not_2_out, D0);
  nand nand_2 (nand_2_out, not_2_out, not_3_out);
  not not_3 (not_3_out, D0);
  JK jk_2 (.J(Q0), .CK(CK), .K(jk_1_nq), .nPR(nand_4_out), .nCLR(nand_3_out), .Q(Q1), .nQ(jk_2_nq));
  nand nand_3 (nand_3_out, not_2_out, not_4_out);
  nand nand_4 (nand_4_out, not_2_out, D1);
  not not_4 (not_4_out, D1);
  JK jk_3 (.J(Q1), .CK(CK), .K(jk_2_nq), .nPR(nand_7_out), .nCLR(nand_5_out), .Q(Q2), .nQ(jk_3_nq));
  nand nand_5 (nand_5_out, not_2_out, not_5_out);
  not not_5 (not_5_out, D2);
  nand nand_6 (nand_6_out, not_2_out, not_6_out);
  nand nand_7 (nand_7_out, not_2_out, D2);
  JK jk_4 (.J(Q2), .CK(CK), .K(jk_3_nq), .nPR(nand_8_out), .nCLR(nand_6_out), .Q(out_12));  // open: nQ
  nand nand_8 (nand_8_out, not_2_out, D3);
  not not_6 (not_6_out, D3);

  assign Q3 = out_12;

  // Notes on the sheet:
  //   PISO
endmodule

module JK (
  input  nPR,
  input  J,
  input  CK,
  input  K,
  input  nCLR,
  output Q,
  output nQ
);

  wire not_1_out, not_2_out;

  J_K_Flip_Flop j_k_ff_1 (.J(J), .clk(CK), .K(K), .Q(Q), .Qn(nQ), .preset(not_1_out), .en(1'b1), .reset(not_2_out));
  not not_1 (not_1_out, nPR);
  not not_2 (not_2_out, nCLR);
endmodule
