// Logisim project sipo.circ as structural Verilog: 1 circuit, main circuit main
module main (
  input  INPUT,
  input  CK,
  output Q0,
  output Q1,
  output Q2,
  output Q3,
  output SERIAL_OUT
);

  wire j_k_ff_1_qn, j_k_ff_2_qn, j_k_ff_3_qn, not_1_out;

  not not_1 (not_1_out, INPUT);
  J_K_Flip_Flop j_k_ff_1 (
    .J(INPUT), .clk(CK), .K(not_1_out), .Q(Q0), .Qn(j_k_ff_1_qn), .en(1'b1));  // open: preset, reset
  J_K_Flip_Flop j_k_ff_2 (
    .J(Q0), .clk(CK), .K(j_k_ff_1_qn), .Q(Q1), .Qn(j_k_ff_2_qn), .en(1'b1));  // open: preset, reset
  J_K_Flip_Flop j_k_ff_3 (
    .J(Q1), .clk(CK), .K(j_k_ff_2_qn), .Q(Q2), .Qn(j_k_ff_3_qn), .en(1'b1));  // open: preset, reset
  J_K_Flip_Flop j_k_ff_4 (.J(Q2), .clk(CK), .K(j_k_ff_3_qn), .Q(Q3), .en(1'b1));  // open: Qn, preset, reset

  assign SERIAL_OUT = Q3;

  // Notes on the sheet:
  //   SIPO
endmodule
